// Logisim project FALCON_08.circ as structural Verilog: 8 circuits, main circuit main
module main (
  input  in_1
);

  wire ALU_ZERO, ALUSRC, CLOCK, MEM_READ, MEM_TO_REG, MEM_WRITE, PC_SRC, REG_WRITE, SEL_RS2;
  wire [1:0] IMM_SELETOR;
  wire [2:0] ALU_OPERATION, FUNCT, RD, RS1, RS2, RS2_VALUE;
  wire [3:0] OPCODE;
  wire [5:0] B_OFFSET, I_OFFSET, S_OFFSET;
  wire [7:0] ALUSRC_DATA, DADO, DADO_REG, IMEDIATO, MEM_DATA, RD1, RD2, RD_STORE;
  wire [8:0] J_OFFSET;
  wire [15:0] instruction_fetch_1_instrucao;

  Clock clock_1 (.out(CLOCK));
  INSTRUCTION_FETCH instruction_fetch_1 (
    .CLOCK(CLOCK), .RESET(in_1), .PC_SRC(PC_SRC), .IMEDIATO(IMEDIATO),
    .INSTRUCAO(instruction_fetch_1_instrucao));
  // Probe on instruction_fetch_1_instrucao
  INSTRUCTION_DECODE instruction_decode_1 (
    .INSTRUCAO(instruction_fetch_1_instrucao), .FUNCT(FUNCT), .RS2(RS2), .RS1(RS1), .RD(RD), .OPCODE(OPCODE),
    .I_OFFSET(I_OFFSET), .S_OFFSET(S_OFFSET), .B_OFFSET(B_OFFSET), .J_OFFSET(J_OFFSET));
  Multiplexer #(.width(3)) multiplexer_1 (.in0(RS2), .in1(RD), .out(RS2_VALUE), .sel(SEL_RS2));
  BANCO_REGISTRADORES banco_registradores_1 (
    .RS1(RS1), .RS2(RS2_VALUE), .RD(RD), .DADO(DADO_REG), .REG_WRITE(REG_WRITE), .CLOCK(CLOCK), .RESET(in_1),
    .RD1(RD1), .RD2(RD2), .RD_STORE(RD_STORE));
  IMM_GEN imm_gen_1 (
    .IMM_SELETOR(IMM_SELETOR), .I_OFFSET(I_OFFSET), .S_OFFSET(S_OFFSET), .B_OFFSET(B_OFFSET),
    .J_OFFSET(J_OFFSET), .IMEDIATO(IMEDIATO));
  UC uc_1 (
    .OPCODE(OPCODE), .FUNCT(FUNCT), .ALU_ZERO(ALU_ZERO), .SINAL_BLT(DADO[0]), .CLOCK(CLOCK),
    .IMM_SELETOR(IMM_SELETOR), .ALUSRC(ALUSRC), .ALUOP(ALU_OPERATION), .SEL_RS2(SEL_RS2),
    .MEM_READ(MEM_READ), .MEM_TO_REG(MEM_TO_REG), .MEM_WRITE(MEM_WRITE), .REG_WRITE(REG_WRITE),
    .PC_SRC(PC_SRC));
  Multiplexer #(.width(8)) multiplexer_2 (.in0(RD2), .in1(IMEDIATO), .out(ALUSRC_DATA), .sel(ALUSRC));
  ULA ula_1 (.SRC1(RD1), .SRC2(ALUSRC_DATA), .ALU_OPERATION(ALU_OPERATION), .RESULT(DADO), .ALU_ZERO(ALU_ZERO));
  Multiplexer #(.width(8)) multiplexer_3 (.in0(DADO), .in1(MEM_DATA), .out(DADO_REG), .sel(MEM_TO_REG));
  DATA_MEMORY data_memory_1 (
    .ENDERECO(DADO), .WRITE_ENABLE(MEM_WRITE), .MEM_READ(MEM_READ), .WRITE_DATA(RD_STORE), .CLOCK(CLOCK),
    .READ_DATA(MEM_DATA));
  // Probe on MEM_DATA

  // Other names for the same wires on the sheet: DADO_B0_BLT = DADO[0]; RESET = in_1
endmodule

module INSTRUCTION_FETCH (
  input  CLOCK,
  input  RESET,
  input  PC_SRC,
  input  [7:0] IMEDIATO,
  output [15:0] INSTRUCAO
);

  wire [7:0] adder_1_out, PC_ATUAL, PC_NORMAL, PROXIMO_PC;

  Adder adder_1 (.a(IMEDIATO), .b(PC_ATUAL), .out(adder_1_out));  // open: cin, cout
  Register PC (.D(PROXIMO_PC), .en(1'b1), .clk(CLOCK), .Q(PC_ATUAL), .clr(RESET));
  Multiplexer #(.width(8)) multiplexer_1 (.in0(PC_NORMAL), .in1(adder_1_out), .out(PROXIMO_PC), .sel(PC_SRC));
  Adder adder_2 (.a(8'h2), .b(PC_ATUAL), .out(PC_NORMAL));  // open: cin, cout
  // ROM #(.line("dual")) rom_1: pin names not known; wires that end beside it: PC_ATUAL

  // Notes on the sheet:
  //   contents of rom_1 (hex, n*v repeats v):
  //   0 0 22 b 24 e 26 f 18 a 87 5 18 14 88 c6 e 80 60 10 1a 1 e 6e 60 d 7e 41 1a 1e 79 42 1c 1 b f6 d 36
  //   8b 86 f 0 1a 1f 7b 43 1b 47 60 2 7b c1 3a 16 3e 17 40 25
endmodule

module INSTRUCTION_DECODE (
  input  [15:0] INSTRUCAO,
  output [2:0] FUNCT,
  output [2:0] RS2,
  output [2:0] RS1,
  output [2:0] RD,
  output [3:0] OPCODE,
  output [5:0] I_OFFSET,
  output [5:0] S_OFFSET,
  output [5:0] B_OFFSET,
  output [8:0] J_OFFSET
);


  assign B_OFFSET = INSTRUCAO[5:0];
  assign FUNCT = INSTRUCAO[2:0];
  assign I_OFFSET = INSTRUCAO[5:0];
  assign J_OFFSET = INSTRUCAO[8:0];
  assign OPCODE = INSTRUCAO[15:12];
  assign RD = INSTRUCAO[11:9];
  assign RS1 = INSTRUCAO[8:6];
  assign RS2 = INSTRUCAO[5:3];
  assign S_OFFSET = INSTRUCAO[5:0];

  // Other names for the same wires on the sheet: B_OFFSETT[5:0] = INSTRUCAO[5:0]; J_OFFSETT[8:0] = INSTRUCAO[8:0];
  //   S_OFFSETT[5:0] = INSTRUCAO[5:0]

  // Notes on the sheet:
  //   ENTRADAS INSTRUCAO
  //   IMEDIATO TIPO I
  //   _______________________________
  //   IMEDIATO TIPO S
  //   ________________________________________________________________________________________
  //   TIPOS INSTRUCAO
  //   ________________________________________________________________________________________
  //   SAÍDAS SEPARADAS
  //   IMEDIATO TIPO B
  //   IMEDIATO TIPO J
  //   _______________________________
endmodule

module BANCO_REGISTRADORES (
  input  [2:0] RS1,
  input  [2:0] RS2,
  input  [2:0] RD,
  input  [7:0] DADO,
  input  REG_WRITE,
  input  CLOCK,
  input  RESET,
  output [7:0] RD1,
  output [7:0] RD2,
  output [7:0] RD_STORE
);

  wire WE_x1, WE_x2, WE_x3, WE_x4, WE_x5, WE_x6, WE_x7;
  wire [7:0] Q_x0, Q_x1, Q_x2, Q_x3, Q_x4, Q_x5, Q_x6, Q_x7;

  Demultiplexer #(.select(3)) demultiplexer_1 (
    .out1(WE_x1), .out2(WE_x2), .out3(WE_x3), .out4(WE_x4), .out5(WE_x5), .out6(WE_x6), .out7(WE_x7),
    .in(REG_WRITE), .sel(RD));  // open: out0
  Register #(.trigger("falling")) x0 (.D({8{1'b0}}), .clk(CLOCK), .Q(Q_x0), .clr(RESET));  // open: en
  Register #(.trigger("falling")) x4 (.D(DADO), .en(WE_x4), .clk(CLOCK), .Q(Q_x4), .clr(RESET));
  Register #(.trigger("falling")) x1 (.D(DADO), .en(WE_x1), .clk(CLOCK), .Q(Q_x1), .clr(RESET));
  Register #(.trigger("falling")) x5 (.D(DADO), .en(WE_x5), .clk(CLOCK), .Q(Q_x5), .clr(RESET));
  Multiplexer #(.select(3), .width(8)) multiplexer_1 (
    .in0(Q_x0), .in1(Q_x1), .in2(Q_x2), .in3(Q_x3), .in4(Q_x4), .in5(Q_x5), .in6(Q_x6), .in7(Q_x7),
    .out(RD1), .sel(RS1));
  Multiplexer #(.select(3), .width(8)) multiplexer_2 (
    .in0(Q_x0), .in1(Q_x1), .in2(Q_x2), .in3(Q_x3), .in4(Q_x4), .in5(Q_x5), .in6(Q_x6), .in7(Q_x7),
    .out(RD2), .sel(RS2));
  Multiplexer #(.select(3), .width(8)) multiplexer_3 (
    .in0(Q_x0), .in1(Q_x1), .in2(Q_x2), .in3(Q_x3), .in4(Q_x4), .in5(Q_x5), .in6(Q_x6), .in7(Q_x7),
    .out(RD_STORE), .sel(RD));
  Register #(.trigger("falling")) x2 (.D(DADO), .en(WE_x2), .clk(CLOCK), .Q(Q_x2), .clr(RESET));
  Register #(.trigger("falling")) x6 (.D(DADO), .en(WE_x6), .clk(CLOCK), .Q(Q_x6), .clr(RESET));
  Register #(.trigger("falling")) x3 (.D(DADO), .en(WE_x3), .clk(CLOCK), .Q(Q_x3), .clr(RESET));
  Register #(.trigger("falling")) x7 (.D(DADO), .en(WE_x7), .clk(CLOCK), .Q(Q_x7), .clr(RESET));

  // Notes on the sheet:
  //   "ESCRITOR" DOS REGISTRADORES
  //   SAÍDA DOS REGISTRADORES
endmodule

module ULA (
  input  [7:0] SRC1,
  input  [7:0] SRC2,
  input  [2:0] ALU_OPERATION,
  output [7:0] RESULT,
  output ALU_ZERO
);

  wire comparator_1_lt;
  wire [7:0] ADD, AND_LOGICO, OR_LOGICO, SLL_LOGICO, SLT_LOGICO, SRL_LOGICO, SUB;

  Adder adder_1 (.a(SRC1), .b(SRC2), .out(ADD));  // open: cin, cout
  Subtractor subtractor_1 (.a(SRC1), .b(SRC2), .out(SUB));  // open: bin, bout
  assign OR_LOGICO = SRC1 | SRC2;  // OR_Gate or_1, 8 bits wide
  assign AND_LOGICO = SRC1 & SRC2;  // AND_Gate and_1, 8 bits wide
  Comparator comparator_1 (.a(SRC1), .b(SRC2), .lt(comparator_1_lt));  // open: gt, eq
  Shifter shifter_1 (.in(SRC1), .\dist (SRC2[2:0]), .out(SLL_LOGICO));
  Shifter #(.shift("lr")) shifter_2 (.in(SRC1), .\dist (SRC2[2:0]), .out(SRL_LOGICO));
  assign SLT_LOGICO = {{7{1'b0}}, comparator_1_lt};  // Bit_Extender bit_extender_1
  Multiplexer #(.select(3), .width(8)) multiplexer_1 (
    .in0(ADD), .in1(SUB), .in2(AND_LOGICO), .in3(OR_LOGICO), .in4(SLT_LOGICO), .in5(SLL_LOGICO),
    .in6(SRL_LOGICO), .out(RESULT), .sel(ALU_OPERATION));  // open: in7
  Comparator comparator_2 (.a({8{1'b0}}), .b(RESULT), .eq(ALU_ZERO));  // open: gt, lt

  // Other names for the same wires on the sheet: ALUOP[2:0] = ALU_OPERATION; ZERO = ALU_ZERO
endmodule

module IMM_GEN (
  input  [1:0] IMM_SELETOR,
  input  [5:0] I_OFFSET,
  input  [5:0] S_OFFSET,
  input  [5:0] B_OFFSET,
  input  [8:0] J_OFFSET,
  output [7:0] IMEDIATO
);

  wire [7:0] B_8B, I_8B, J_8B, S_8B;

  assign I_8B = {{2{I_OFFSET[5]}}, I_OFFSET};  // Bit_Extender bit_extender_1
  assign S_8B = {{2{S_OFFSET[5]}}, S_OFFSET};  // Bit_Extender bit_extender_2
  // Probe on B_8B
  assign B_8B = {{1{B_OFFSET[5]}}, {B_OFFSET, 1'b0}};  // Bit_Extender bit_extender_3
  // Probe on J_8B
  Bit_Extender #(.in_width(10), .out_width(8)) bit_extender_4 (.in({J_OFFSET, 1'b0}), .out(J_8B));
  Multiplexer #(.select(2), .width(8)) multiplexer_1 (
    .in0(I_8B), .in1(S_8B), .in2(B_8B), .in3(J_8B), .out(IMEDIATO), .sel(IMM_SELETOR));

  // Other names for the same wires on the sheet: RESULTADO_IMEDIATO[7:0] = IMEDIATO

  // Notes on the sheet:
  //   INSTRUCAO TIPO I
  //   INSTRUCAO TIPO S
  //   INSTRUCAO TIPO B
  //   INSTRUCAO TIPO J
endmodule

module UC (
  input  [3:0] OPCODE,
  input  [2:0] FUNCT,
  input  ALU_ZERO,
  input  SINAL_BLT,
  input  CLOCK,
  output [1:0] IMM_SELETOR,
  output ALUSRC,
  output [2:0] ALUOP,
  output SEL_RS2,
  output MEM_READ,
  output MEM_TO_REG,
  output MEM_WRITE,
  output REG_WRITE,
  output PC_SRC
);

  wire and_1_out, and_2_out, and_3_out, comparator_1_eq, comparator_2_eq, comparator_3_eq, not_1_out,
       not_2_out, OFFSET_TIPO_B, OFFSET_TIPO_I, TIPO_B, TIPO_B_NOT_EQUAL, TIPO_B_OFFSET, TIPO_I, TIPO_I_LOAD,
       TIPO_I_SLLI, TIPO_J, TIPO_R;
  wire [3:0] rom_1_data;

  or or_1 (OFFSET_TIPO_I, TIPO_I_SLLI, TIPO_I, TIPO_I_LOAD);
  or or_2 (OFFSET_TIPO_B, TIPO_B_NOT_EQUAL, TIPO_B, TIPO_B_OFFSET);
  ROM #(.addrWidth(4), .dataWidth(4)) rom_1 (.addr(OPCODE), .data(rom_1_data));
  or or_3 (REG_WRITE, OFFSET_TIPO_I, TIPO_R, TIPO_J);
  Decoder #(.select(4)) decoder_1 (
    .out0(TIPO_R), .out1(TIPO_I), .out2(TIPO_I_LOAD), .out3(MEM_WRITE), .out4(TIPO_B),
    .out5(TIPO_B_NOT_EQUAL), .out6(TIPO_J), .out7(TIPO_I_SLLI), .out8(TIPO_B_OFFSET), .sel(OPCODE), .en(1'b1));  // open: out9, out10, out11, out12, out13, out14, out15
  or or_4 (IMM_SELETOR[0], MEM_WRITE, TIPO_J);
  or or_5 (IMM_SELETOR[1], OFFSET_TIPO_B, TIPO_J);
  or or_6 (SEL_RS2, OFFSET_TIPO_B, TIPO_I_LOAD);
  // Probe on IMM_SELETOR
  Multiplexer #(.width(3)) multiplexer_1 (.in0(FUNCT), .in1(rom_1_data[3:1]), .out(ALUOP), .sel(rom_1_data[0]));
  or or_7 (ALUSRC, OFFSET_TIPO_I, MEM_WRITE);
  or or_8 (MEM_READ, MEM_WRITE, TIPO_I_LOAD);
  // Probe on ALUSRC
  Comparator #(.width(4)) comparator_1 (.a(4'b0100), .b(OPCODE), .eq(comparator_1_eq));  // open: gt, lt
  Comparator #(.width(4)) comparator_2 (.a(4'b0101), .b(OPCODE), .eq(comparator_2_eq));  // open: gt, lt
  Comparator #(.width(4)) comparator_3 (.a(4'b1000), .b(OPCODE), .eq(comparator_3_eq));  // open: gt, lt
  not not_1 (not_1_out, ALU_ZERO);
  not not_2 (not_2_out, SINAL_BLT);
  and and_1 (and_1_out, ALU_ZERO, comparator_1_eq);
  and and_2 (and_2_out, not_1_out, comparator_2_eq);
  and and_3 (and_3_out, not_2_out, comparator_3_eq);
  or or_9 (PC_SRC, and_1_out, and_2_out, and_3_out, TIPO_J);

  assign MEM_TO_REG = MEM_READ;

  // Other names for the same wires on the sheet: MEMREAD = MEM_READ; TIPO_S = MEM_WRITE

  // Notes on the sheet:
  //   GERADOR DO IMM SELECTOR
  //   GERADOR DO ALUOP 
  //   contents of rom_1 (hex, n*v repeats v):
  //   0 1 1 1 3 3 1 b 9
  //   GERADOR REG WRITE
  //   GERADOR RS2 DE BRANCHS
  //   GERADOR ALUSRC
  //   GERADOR MEM READ
  //   SAÍDAS
  //   BLT
  //   GERADOR PC_SRC
  //   BEQ
  //   BNE
  //   JAL
endmodule

module DATA_MEMORY (
  input  [7:0] ENDERECO,
  input  WRITE_ENABLE,
  input  MEM_READ,
  input  [7:0] WRITE_DATA,
  input  CLOCK,
  output [7:0] READ_DATA
);

  wire [7:0] ram_1_dout;

  RAM #(.asyncread("true"), .trigger("falling")) ram_1 (
    .addr(ENDERECO), .we(WRITE_ENABLE), .oe(MEM_READ), .clk(CLOCK), .din(WRITE_DATA), .dout(ram_1_dout));
  assign READ_DATA = MEM_READ ? ram_1_dout : 8'bz;  // Controlled_Buffer controlled_buffer_1

  // Other names for the same wires on the sheet: ENDENRECO[7:0] = ENDERECO
endmodule
